# Fritzing sketch KY-022_ESP32 (saved by Fritzing 0.9.10b)

parts:
  Part1 = KY-022 Infrared Receiver Module [package="Breakout board"]
  U1 = ESP32-38PinWide [part_number=ESP32-38PinWide]

nets:
  N1: Part1.S, U1.GPIO23
  N2: Part1.Vin, U1.3.3
  N3: Part1.-, U1.GND

notes:
  GPIO 23
  3V3
  Pin central (VCC)
  Pin Signal
  Pin GND
  GND
  KY-022: Módulo receptor de infrarrojos
  Raspberry Pi Buenos Aires

custom parts:
  KY-022 Infrared Receiver Module: Arduino IR receiver module KY-022, reacts to 38kHz infrared light.
  ESP32-38PinWide: Generic 38-Pin ESP32 with wide format (only access to one side of pins on a breadboard) based on Stephen Lilley's HiLetgo ESP-WROOM-32 ESP32 ESP-32S Development Board.
