# Fritzing sketch KY-022_ESP32_ejemplo_uso (saved by Fritzing 0.9.10b)
breadboards: 1

parts:
  Part1 = KY-022 Infrared Receiver Module [package="Breakout board"]
  U1 = ESP32-38PinWide [part_number=ESP32-38PinWide]
  LED1 = LED - 5mm [color="Orange (612nm)" current=0.030 package="5 mm [THT]"]
  LED2 = LED - 5mm [color="Green (555nm)" current=0.030 package="5 mm [THT]"]
  LED3 = LED - 5mm [color="Red (633nm)" current=0.030 package="5 mm [THT]"]
  LED4 = LED - 5mm [color="Blue (430nm)" current=0.030 package="5 mm [THT]"]

nets:
  N1: Part1.S, U1.GPIO23
  N2: Part1.Vin, U1.3.3
  N3: Part1.-, U1.GND, LED1.cathode, LED2.cathode, LED3.cathode, LED4.cathode
  N4: U1.GPIO16, LED1.anode
  N5: U1.GPIO17, LED2.anode
  N6: U1.GPIO5, LED3.anode
  N7: U1.GPIO18, LED4.anode

notes:
  GPIO 23
  3V3
  Pin central (VCC)
  Pin Signal
  Pin GND
  GND
  KY-022: Módulo receptor de infrarrojos
  Raspberry Pi Buenos Aires
  Anodo
  Catodo
  GPIO 18
  GPIO 5
  GPIO 17
  GPIO 16

custom parts:
  KY-022 Infrared Receiver Module: Arduino IR receiver module KY-022, reacts to 38kHz infrared light.
  ESP32-38PinWide: Generic 38-Pin ESP32 with wide format (only access to one side of pins on a breadboard) based on Stephen Lilley's HiLetgo ESP-WROOM-32 ESP32 ESP-32S Development Board.
