# Fritzing sketch KY-001 (saved by Fritzing 0.9.3b)

parts:
  Part1 = KY-001 Temperature Sensor Module [package="Breakout board"]
  Part2 = Arduino Uno (Rev3)

nets:
  N1: Part1.S, Part2.D2
  VIN: Part1.Vin, Part2.5V
  N2: Part1.-, Part2.GND

notes:
  KY-001: Módulo sensor de temperatura DS18B20
  VCC
  SIGNAL
  GND
  5V
  Pin 2

custom parts:
  KY-001 Temperature Sensor Module: Arduino Temperature Sensor Module Keyes KY-001, Allows ambient temperature measurement using digital serial bus (DS18B20)
