# Fritzing sketch KY-001pi (saved by Fritzing 0.9.3b)

parts:
  Part1 = KY-001 Temperature Sensor Module [package="Breakout board"]
  Raspberry_Pi_1 = Raspberry Pi 3 [part_number=RPI-3-V1.2]

nets:
  N1: Part1.S, Raspberry_Pi_1.GIPO4
  VIN: Part1.Vin, Raspberry_Pi_1.3v3
  N2: Part1.-, Raspberry_Pi_1.GND

notes:
  KY-001: Módulo sensor de temperatura DS18B20
  VCC
  SIGNAL
  GND
  3.3V Pin fisico 1
  GPIO 4 Pin fisico 7
  GND Pin fisico 6

custom parts:
  KY-001 Temperature Sensor Module: Arduino Temperature Sensor Module Keyes KY-001, Allows ambient temperature measurement using digital serial bus (DS18B20)
