# Fritzing sketch KY-002 (saved by Fritzing 0.9.3b)

parts:
  Part1 = KY-002 Vibration Switch Module [package="Breakout board"]
  Componente1 = Arduino Uno (Rev3)

nets:
  N1: Part1.S, Componente1.D10_PWM/SS
  VIN: Part1.Vin, Componente1.5V
  N2: Part1.-, Componente1.GND

notes:
  PIN DIGITAL 10
  PIN S
  GND
  PIN +
  5V
  KY-002 : Módulo Sensor de Vibración

custom parts:
  KY-002 Vibration Switch Module: Arduino Vibration Switch Module KY-002 Keyes allows detection of shock and vibration.
