# Fritzing sketch KY-002pi (saved by Fritzing 0.9.3b)

parts:
  Part1 = KY-002 Vibration Switch Module [package="Breakout board"]
  Raspberry_Pi_1 = Raspberry Pi 3 [part_number=RPI-3-V1.2]

nets:
  N1: Part1.S, Raspberry_Pi_1.GIPO24
  VIN: Part1.Vin, Raspberry_Pi_1.3v3
  N2: Part1.-, Raspberry_Pi_1.GND

notes:
  PIN 18 GPIO24
  PIN S
  GND
  PIN 6 GND
  PIN +
  PIN 1 3.3V
  KY-002 : Módulo Sensor de Vibración

custom parts:
  KY-002 Vibration Switch Module: Arduino Vibration Switch Module KY-002 Keyes allows detection of shock and vibration.
