# Fritzing sketch KY-003 (saved by Fritzing 0.9.3b)

parts:
  Componente1 = Arduino Uno (Rev3)
  Part1 = KY-003 Hall Magnetic Sensor Module [package="Breakout board"]

nets:
  N1: Componente1.D10_PWM/SS, Part1.S
  N2: Componente1.GND, Part1.-
  5V: Componente1.5V, Part1.Vin

notes:
  Pin 10 Arduino
  5V Arduino
  Pin central Sensor
  Pin Signal Sensor
  Pin - Sensor
  GND Arduino
  KY-003: Módulo Sensor Efecto Hall
  https://www.facebook.com/groups/RaspberryPiBuenosAires

custom parts:
  KY-003 Hall Magnetic Sensor Module: KEYES KY-003 Arduino Hall Magnetic Sensor Module is a switch that will turn on/off in the presence of a magnetic field.
