# Fritzing sketch KY-003pi (saved by Fritzing 0.9.3b)

parts:
  Part1 = KY-003 Hall Magnetic Sensor Module [package="Breakout board"]
  Raspberry_Pi_1 = Raspberry Pi 3 [part_number=RPI-3-V1.2]

nets:
  N1: Part1.S, Raspberry_Pi_1.GIPO24
  VIN: Part1.Vin, Raspberry_Pi_1.3v3
  N2: Part1.-, Raspberry_Pi_1.GND

notes:
  Pin 18 GPIO24 Raspberry Pi
  3.3V Pin 1 Raspberry Pi
  Pin central Sensor
  Pin Signal Sensor
  Pin - Sensor
  GND Pin 6 Raspberry Pi
  KY-003: Módulo Sensor Efecto Hall
  https://www.facebook.com/groups/RaspberryPiBuenosAires

custom parts:
  KY-003 Hall Magnetic Sensor Module: KEYES KY-003 Arduino Hall Magnetic Sensor Module is a switch that will turn on/off in the presence of a magnetic field.
