# Fritzing sketch KY-004 (saved by Fritzing 0.9.3b)

parts:
  Part1 = KY-004 Key Switch Module [package="Breakout board"]
  Componente1 = Arduino Uno (Rev3)

nets:
  N1: Part1.S, Componente1.D10_PWM/SS
  VIN: Part1.Vin, Componente1.5V
  N2: Part1.-, Componente1.GND

notes:
  Pin 10 Arduino
  5V Arduino
  Pin central
  Pin Signal
  Pin -
  GND Arduino
  KY-004: Módulo botón interruptor
  https://www.facebook.com/groups/RaspberryPiBuenosAires

custom parts:
  KY-004 Key Switch Module: Arduino Key Switch Module Keyes KY-004 is a push button that will output a high signal when pressed.
