# Fritzing sketch KY-004pi (saved by Fritzing 0.9.3b)

parts:
  Raspberry_Pi_1 = Raspberry Pi 3 [part_number=RPI-3-V1.2]
  Part1 = KY-004 Key Switch Module [package="Breakout board"]

nets:
  3V3: Raspberry_Pi_1.3v3, Part1.Vin
  N1: Raspberry_Pi_1.GIPO24, Part1.S
  N2: Raspberry_Pi_1.GND, Part1.-

notes:
  Pin 18 GPIO24 Raspberry Pi
  3.3V Pin 1 Raspberry Pi
  Pin central
  Pin Signal
  Pin -
  GND Pin 6 Raspberry Pi
  KY-004: Módulo botón interruptor
  https://www.facebook.com/groups/RaspberryPiBuenosAires

custom parts:
  KY-004 Key Switch Module: Arduino Key Switch Module Keyes KY-004 is a push button that will output a high signal when pressed.
