# Fritzing sketch KY-005 (saved by Fritzing 0.9.3b)

parts:
  Componente1 = Arduino Uno (Rev3)
  Part1 = KY-005 Infrared Transmitter Module [package="Breakout board"]

nets:
  N1: Componente1.GND, Part1.-
  N2: Componente1.D3_PWM, Part1.S
  5V: Componente1.5V, Part1.Vin

notes:
  Pin 3 Arduino declarado por la librería
  5V Arduino
  Pin central
  Pin Signal
  Pin -
  GND Arduino
  KY-005: Módulo transmisor de infrarrojos
  Raspberry Pi Buenos Aires

custom parts:
  KY-005 Infrared Transmitter Module: Arduino IR Transmitter Module Keyes KY-005, emits infrared light at 38KHz.
