# Fritzing sketch KY-005pi (saved by Fritzing 0.9.3b)

parts:
  Raspberry_Pi_1 = Raspberry Pi 3 [part_number=RPI-3-V1.2]
  Part1 = KY-005 Infrared Transmitter Module [package="Breakout board"]
  R1 = Resistor [tolerance=±5% resistance=10k package=THT]
  PNP_2N2222 = NPN-Transistor [package="TO92 [THT]"]

nets:
  N1: Raspberry_Pi_1.3v3, R1.Pin_1
  N2: Raspberry_Pi_1.GND, PNP_2N2222.E
  N3: Raspberry_Pi_1.GIPO17, Part1.S
  N4: Part1.Vin, PNP_2N2222.C

notes:
  Pin 11 GPIO17 Raspberry Pi
  3.3V Raspberry Pi
  Pin central Sensor
  Pin Signal Sensor
  Pin - Sensor
  GND Pin 6 Raspberry Pi
  KY-005: Módulo Transmisor Infrarrojos
  E
  B
  C
  Raspberry Pi Buenos Aires

custom parts:
  KY-005 Infrared Transmitter Module: Arduino IR Transmitter Module Keyes KY-005, emits infrared light at 38KHz.
