# Fritzing sketch KY-006 (saved by Fritzing 0.9.3b)

parts:
  Componente1 = Arduino Uno (Rev3)
  Part1 = KY-006 Passive Buzzer Module [package="Breakout board"]

nets:
  N1: Componente1.D8, Part1.S
  N2: Componente1.GND, Part1.-

notes:
  Pin 8 Arduino
  Pin central No Conectado
  Pin Signal
  Pin -
  GND Arduino
  KY-006: Módulo buzzer-Piezo pasivo

custom parts:
  KY-006 Passive Buzzer Module: Passive Piezoelectric Buzzer Module Keyes KY-006, it can produce a range of sound tones depending on the input frequency.
