# Fritzing sketch KY-006pi (saved by Fritzing 0.9.3b)

parts:
  Raspberry_Pi_1 = Raspberry Pi 3 [part_number=RPI-3-V1.2]
  Part1 = KY-006 Passive Buzzer Module [package="Breakout board"]

nets:
  N1: Raspberry_Pi_1.GIPO24, Part1.S
  N2: Raspberry_Pi_1.GND, Part1.-

notes:
  Pin 18 GPIO24 Raspberry Pi
  3.3V Pin 1 Raspberry Pi
  Pin central Sensor
  Pin Signal Sensor
  Pin - Sensor
  GND Pin 6 Raspberry Pi
  KY-006: Módulo Buzzer-Piezo pasivo

custom parts:
  KY-006 Passive Buzzer Module: Passive Piezoelectric Buzzer Module Keyes KY-006, it can produce a range of sound tones depending on the input frequency.
