# Fritzing sketch KY-008 (saved by Fritzing 0.9.3b)

parts:
  Part1 = KY-008 Laser Transmitter Module [package="Breakout board"]
  Componente1 = Arduino Uno (Rev3)

nets:
  N1: Part1.S, Componente1.D13/SCK
  N2: Part1.-, Componente1.GND

notes:
  Pin 13 Arduino
  Pin - Sensor
  GND Arduino
  KY-008: Módulo Laser
  Pin Central no se conecta
  Pin S

custom parts:
  KY-008 Laser Transmitter Module: Laser Transmitter module KY-008 for Arduino, emits a dot shaped red laser beam.
