# Fritzing sketch KY-008pi (saved by Fritzing 0.9.3b)

parts:
  Raspberry_Pi_1 = Raspberry Pi 3 [part_number=RPI-3-V1.2]
  Part1 = KY-008 Laser Transmitter Module [package="Breakout board"]

nets:
  N1: Raspberry_Pi_1.GND, Part1.-
  N2: Raspberry_Pi_1.5V, Part1.S

notes:
  5V Pin 2 Raspberry Pi
  Pin - Sensor
  GND Pin 6 Raspberry Pi
  KY-008: Módulo Laser
  Pin Centra no se conecta
  Pin S

custom parts:
  KY-008 Laser Transmitter Module: Laser Transmitter module KY-008 for Arduino, emits a dot shaped red laser beam.
