# Fritzing sketch KY-009 (saved by Fritzing 0.9.3b)

parts:
  Componente1 = Arduino Uno (Rev3)
  Part1 = KY-009 Full Color RGB LED SMD Module [package="Breakout board"]

nets:
  N1: Componente1.D9_PWM, Part1.R
  N2: Componente1.D10_PWM/SS, Part1.G
  N3: Componente1.D11_PWM/MOSI, Part1.B
  N4: Componente1.GND, Part1.-

notes:
  Pin 9 Arduino
  Pin B
  Pin -
  GND Arduino
  KY-009: Módulo LED RGB SMD
  Pin G
  Pin R
  Pin 11 Arduino
  Pin 10 Arduino

custom parts:
  KY-009 Full Color RGB LED SMD Module: RGB full color LED Module KY-009 for Arduino, emits a range of colors by mixing red, green and blue. The amount of each primary color is adjusted using PWM.
