# Fritzing sketch KY-009pi (saved by Fritzing 0.9.3b)

parts:
  Raspberry_Pi_1 = Raspberry Pi 3 [part_number=RPI-3-V1.2]
  Part1 = KY-009 Full Color RGB LED SMD Module [package="Breakout board"]

nets:
  N1: Raspberry_Pi_1.GIPO22, Part1.R
  N2: Raspberry_Pi_1.GIPO16, Part1.B
  N3: Raspberry_Pi_1.GIPO24, Part1.G
  N4: Raspberry_Pi_1.GND, Part1.-

notes:
  Pin 18 GPIO24 Raspberry Pi
  Pin 15 GPIO22 Raspberry Pi
  Pin - Sensor
  GND Pin 6 Raspberry Pi
  KY-009: Módulo LED SMD RGB
  Pin 36 GPIO16 Raspberry Pi
  Pin B
  Pin G
  Pin R

custom parts:
  KY-009 Full Color RGB LED SMD Module: RGB full color LED Module KY-009 for Arduino, emits a range of colors by mixing red, green and blue. The amount of each primary color is adjusted using PWM.
