# Fritzing sketch KY-010 (saved by Fritzing 0.9.3b)

parts:
  Componente1 = Arduino Uno (Rev3)
  Part1 = KY-010 Photo Interrupter Module [package="Breakout board"]

nets:
  N1: Componente1.D10_PWM/SS, Part1.S
  N2: Componente1.GND, Part1.-
  5V: Componente1.5V, Part1.Vin

notes:
  Pin 10 Arduino
  5V Arduino
  Pin central Sensor
  Pin Signal Sensor
  Pin - Sensor
  GND Arduino
  KY-010: Módulo Sensor Barrera óptica

custom parts:
  KY-010 Photo Interrupter Module: Photo Interrupter Module Keyes KY-010 for Arduino, will trigger a signal when light between the sensor's gap is blocked.
