# Fritzing sketch KY-010pi (saved by Fritzing 0.9.3b)

parts:
  Raspberry_Pi_1 = Raspberry Pi 3 [part_number=RPI-3-V1.2]
  Part1 = KY-010 Photo Interrupter Module [package="Breakout board"]

nets:
  3V3: Raspberry_Pi_1.3v3, Part1.Vin
  N1: Raspberry_Pi_1.GIPO24, Part1.S
  N2: Raspberry_Pi_1.GND, Part1.-

notes:
  Pin 18 GPIO24 Raspberry Pi
  3.3V Pin 1 Raspberry Pi
  Pin central Sensor
  Pin Signal Sensor
  Pin - Sensor
  GND Pin 6 Raspberry Pi
  KY-010: Módulo Sensor Barrera óptica

custom parts:
  KY-010 Photo Interrupter Module: Photo Interrupter Module Keyes KY-010 for Arduino, will trigger a signal when light between the sensor's gap is blocked.
