# Fritzing sketch KY-011 (saved by Fritzing 0.9.3b)

parts:
  Componente1 = Arduino Uno (Rev3)
  Part1 = KY-011 Two Color LED Module [package="Breakout board"]
  R2 = Resistor [tolerance=±5% resistance=330 package=THT]
  R1 = Resistor [tolerance=±5% resistance=330 package=THT]

nets:
  N1: Componente1.D10_PWM/SS, R1.Pin_1
  N2: Componente1.D11_PWM/MOSI, R2.Pin_1
  N3: Componente1.GND, Part1.-

notes:
  Pin 10 Arduino
  Pin 11 Arduino
  Pin central Sensor
  Pin Signal Sensor
  Pin - Sensor
  GND Arduino
  KY-011: Módulo Led Bicolor

custom parts:
  KY-011 Two Color LED Module: KEYES KY-011 Two Color LED Module consist of a common cathode 3mm red/green LED.
