# Fritzing sketch KY-011pi (saved by Fritzing 0.9.3b)

parts:
  Part1 = KY-011 Two Color LED Module [package="Breakout board"]
  R2 = Resistor [tolerance=±5% resistance=150 package=THT]
  R1 = Resistor [tolerance=±5% resistance=150 package=THT]
  Raspberry_Pi_1 = Raspberry Pi 3 [part_number=RPI-3-V1.2]

nets:
  N1: Part1.-, Raspberry_Pi_1.GND
  N2: R2.Pin_1, Raspberry_Pi_1.GIPO16
  N3: R1.Pin_1, Raspberry_Pi_1.GIPO18

notes:
  Pin 12 GPIO18 Raspberry Pi
  Pin 36 GPIO16 Raspberry Pi
  Pin central Sensor
  Pin Signal Sensor
  Pin - Sensor
  GND Arduino
  KY-011: Módulo Led Bicolor

custom parts:
  KY-011 Two Color LED Module: KEYES KY-011 Two Color LED Module consist of a common cathode 3mm red/green LED.
