# Fritzing sketch KY-012 (saved by Fritzing 0.9.3b)

parts:
  Componente1 = Arduino Uno (Rev3)
  Part1 = KY-012 Active Buzzer Module [package="Breakout board"]

nets:
  N1: Componente1.D8, Part1.S
  N2: Componente1.GND, Part1.-

notes:
  Pin 10 Arduino
  Pin Signal Sensor
  Pin - Sensor
  GND Arduino
  KY-012: Módulo Buzzer Activo

custom parts:
  KY-012 Active Buzzer Module: Active Piezoelectric Buzzer Module Keyes KY-012, it produces single-tone sound when signal is high.
