# Fritzing sketch KY-012pi (saved by Fritzing 0.9.3b)

parts:
  Part1 = KY-012 Active Buzzer Module [package="Breakout board"]
  Raspberry_Pi_1 = Raspberry Pi 3 [part_number=RPI-3-V1.2]

nets:
  N1: Part1.S, Raspberry_Pi_1.GIPO18
  N2: Part1.-, Raspberry_Pi_1.GND

notes:
  Pin 12 GPIO18 Raspberry Pi
  Pin Signal Sensor
  Pin - Sensor
  GND Arduino
  KY-012: Módulo Buzzer Activo
  Pin 1 3.3V Raspberry Pi
  Pin Central Modulo

custom parts:
  KY-012 Active Buzzer Module: Active Piezoelectric Buzzer Module Keyes KY-012, it produces single-tone sound when signal is high.
