# Fritzing sketch KY-013 (saved by Fritzing 0.9.3b)

parts:
  Componente1 = Arduino Uno (Rev3)
  Part1 = KY-013 Analog Temperature Sensor Module [package="Breakout board"]

nets:
  N1: Componente1.A0, Part1.S
  N2: Componente1.GND, Part1.-
  5V: Componente1.5V, Part1.Vin

notes:
  Pin A0 Arduino
  5V Arduino
  Pin central Sensor
  Pin Signal Sensor
  Pin - Sensor
  GND Arduino
  KY-013: Módulo Analogo Sensor de Temperatura

custom parts:
  KY-013 Analog Temperature Sensor Module: KY-013 Analog Temperature Sensor module, measures ambient temperature based on resistance of the thermistor.
