# Fritzing sketch KY-015pi (saved by Fritzing 0.9.3b)

parts:
  Part1 = KY-015 Temperature & Humidity Sensor Module [package="Breakout board"]
  Raspberry_Pi_1 = Raspberry Pi 3 [part_number=RPI-3-V1.2]

nets:
  N1: Part1.S, Raspberry_Pi_1.GIPO23
  VIN: Part1.Vin, Raspberry_Pi_1.3v3
  N2: Part1.-, Raspberry_Pi_1.GND

notes:
  GPIO 23 Pin fisico 16
  Pin 1 3.3V
  Pin central Sensor
  Pin Signal Sensor
  Pin - Sensor
  GND Pin 6
  KY-015: Módulo Sensor de Temperatura y Humedad

custom parts:
  KY-015 Temperature & Humidity Sensor Module: KY-015 temperature and humidity sensor module, provides a low-latency serial interface to measure humidity and temperature.
