# Fritzing sketch KY-016 (saved by Fritzing 0.9.3b)

parts:
  Componente1 = Arduino Uno (Rev3)
  Part1 = KY-016 RGB Full Color LED Module [package="Breakout board"]

nets:
  N1: Componente1.D9_PWM, Part1.R
  N2: Componente1.D10_PWM/SS, Part1.G
  N3: Componente1.D11_PWM/MOSI, Part1.B
  N4: Componente1.GND, Part1.-

notes:
  Pin 9 Arduino
  Pin B
  Pin -
  GND Arduino
  KY-016: Módulo LED RGB Tricolor
  Pin G
  Pin R
  Pin 11 Arduino
  Pin 10 Arduino

custom parts:
  KY-016 RGB Full Color LED Module: KY-016 Arduino full color 5mm RGB LED, different colors can be obtained by mixing the three primary colors.
