# Fritzing sketch KY-016pi (saved by Fritzing 0.9.3b)

parts:
  Part1 = KY-016 RGB Full Color LED Module [package="Breakout board"]
  Raspberry_Pi_1 = Raspberry Pi 3 [part_number=RPI-3-V1.2]

nets:
  N1: Part1.-, Raspberry_Pi_1.GND
  N2: Part1.R, Raspberry_Pi_1.GIPO6
  N3: Part1.G, Raspberry_Pi_1.GIPO5
  N4: Part1.B, Raspberry_Pi_1.GIPO4

notes:
  Pin 31 GPIO6 Raspberry Pi
  Pin B
  Pin -
  Pin 6 GND Raspberry Pi
  KY-016: Módulo LED RGB Tricolor
  Pin G
  Pin R
  Pin 7 GPIO4 Raspberry Pi
  Pin 29 GPIO5 Raspberry Pi

custom parts:
  KY-016 RGB Full Color LED Module: KY-016 Arduino full color 5mm RGB LED, different colors can be obtained by mixing the three primary colors.
