# Fritzing sketch KY-017 (saved by Fritzing 0.9.3b)

parts:
  Componente1 = Arduino Uno (Rev3)
  Part1 = KY-017 Mercury Tilt Switch [package="Breakout board"]

nets:
  N1: Componente1.GND, Part1.-
  N2: Componente1.D3_PWM, Part1.S
  5V: Componente1.5V, Part1.Vin

notes:
  Pin 3 Arduino
  5V Arduino
  Pin central Sensor
  Pin Signal Sensor
  Pin - Sensor
  GND Arduino
  KY-017: Módulo Interruptor de Mercurio

custom parts:
  KY-017 Mercury Tilt Switch: Arduino KY-017 mercury tilt switch module, it uses a small mercury ball that completes the circuit when you tilt the module.
