# Fritzing sketch KY-018 (saved by Fritzing 0.9.3b)

parts:
  Componente1 = Arduino Uno (Rev3)
  Part1 = KY-018 Photoresistor Module [package="Breakout board"]

nets:
  N1: Componente1.A3, Part1.S
  N2: Componente1.GND, Part1.-
  5V: Componente1.5V, Part1.Vin

notes:
  Pin A3 Arduino
  5V Arduino
  Pin central Sensor
  Pin Signal Sensor
  Pin - Sensor
  GND Arduino
  KY-018: Módulo Fotoresistor

custom parts:
  KY-018 Photoresistor Module: KY-018 Photoresistor module, used to measure light intensity. It can determine the presence or absence of light.
