# Fritzing sketch KY-018pi (saved by Fritzing 0.9.3b)

parts:
  Componente2 = Adafruit ADS1115 16Bit I2C ADC [part_number="Adafruit #1085"]
  Raspberry_Pi_1 = Raspberry Pi 3 [part_number=RPI-3-V1.2]
  Part1 = KY-018 Photoresistor Module [package="Breakout board"]

nets:
  N1: Componente2.AIN0, Part1.S
  N2: Componente2.SDA, Raspberry_Pi_1.GPIO3
  N3: Componente2.SCL, Raspberry_Pi_1.GPIO2
  GND: Componente2.GND, Raspberry_Pi_1.GND, Part1.-
  3V3: Componente2.VDD, Raspberry_Pi_1.3v3, Raspberry_Pi_1.3V3, Part1.Vin

notes:
  Pin A0 ADS1115
  Pin 1 3.3V Raspberry pi
  Pin central Sensor
  Pin Signal Sensor
  Pin - Sensor
  Pin 6 GND Raspberry Pi
  KY-018: Módulo Analogo Fotoresistor
  Pin GND ADS1115
  Pin VDD ADS1115
  Pin 3 GPIO2 Raspberry Pi
  Pin 5 GPIO3 Raspberry Pi
  Pin 9   GND Raspberry Pi
  Pin 17 3.3V Raspberry pi
  Pin SDA ADS1115
  Pin SCL ADS1115

custom parts:
  Adafruit ADS1115 16Bit I2C ADC: For microcontrollers without an analog-to-digital converter or when you want a higher-precision ADC, the ADS1115 provides 16-bit precision at 860 samples/second over I2C. The chip can be configured as 4 single-ended input channels, or two differential channels. As a nice bonus, it even includes a programmable gain amplifier, up to x16, to help boost up smaller single/differential signals to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
  KY-018 Photoresistor Module: KY-018 Photoresistor module, used to measure light intensity. It can determine the presence or absence of light.
