# Fritzing sketch KY-019 (saved by Fritzing 0.9.3b)

parts:
  Componente1 = Arduino Uno (Rev3)
  Part1 = KY-019 5V Relay Module [package="Breakout board"]
  LED1 = LEDs [package=led10mm]

nets:
  N1: Componente1.D10_PWM/SS, Part1.S
  N2: Componente1.GND, Part1.-
  N3: Componente1.5V, Part1.+
  N4: Part1.NO, LED1.C

notes:
  Pin 10 Arduino
  5V Arduino
  Pin central Sensor
  Pin Signal Sensor
  Pin - Sensor
  GND Arduino
  KY-019: Módulo Relay 5V
  Normally Close
  Normally Open
  Common
  Neutro
  Fase
  220V

custom parts:
  KY-019 5V Relay Module: KY-019 5V Relay module, used to control AC circuits.
  LEDs: LEDs Standard schematic elements and footprints for 5mm, 3mm, 1206, and 0603 sized LEDs. 5mm - Spark Fun Electronics SKU : COM-00529 (and others)
