# Fritzing sketch KY-019pi (saved by Fritzing 0.9.3b)

parts:
  LED1 = LEDs [package=led10mm]
  KY-1 = Keyes Relay [package=THT]
  Raspberry_Pi_1 = Raspberry Pi 3 [part_number=RPI-3-V1.2]

nets:
  N1: LED1.C, KY-1.NO
  N2: KY-1.signal, Raspberry_Pi_1.GIPO24
  N3: KY-1.power, Raspberry_Pi_1.5V
  N4: KY-1.ground, Raspberry_Pi_1.GND

notes:
  Pin 18 GPIO24 Raspberry Pi
  Pin 1 5V Raspberry Pi
  Pin central Sensor
  Pin Signal Sensor
  Pin - Sensor
  Pin 6 GND Raspberry Pi
  KY-019: Módulo Relay 5V
  Normally Close
  Normally Open
  Common
  Neutro
  Fase
  220V

custom parts:
  LEDs: LEDs Standard schematic elements and footprints for 5mm, 3mm, 1206, and 0603 sized LEDs. 5mm - Spark Fun Electronics SKU : COM-00529 (and others)
  Keyes Relay: The Keyes 5V relay module is suitable for SCM development, home appliance control. It uses a 5V~12V TIL control signal which can control DC / AC signal.
