# Fritzing sketch KY-020 (saved by Fritzing 0.9.3b)

parts:
  Componente1 = Arduino Uno (Rev3)
  Part1 = KY-020 Tilt Switch Module [package="Breakout board"]

nets:
  N1: Componente1.GND, Part1.-
  N2: Componente1.D3_PWM, Part1.S
  5V: Componente1.5V, Part1.Vin

notes:
  Pin 3 Arduino
  5V Arduino
  Pin central Sensor
  Pin Signal Sensor
  Pin - Sensor
  GND Arduino
  KY-020: Módulo Interruptor de Inclinación

custom parts:
  KY-020 Tilt Switch Module: KY-020 Arduino tilt switch sensor module. Closes the circuit when it is tilted to the side as long as it is moved with enough force and degree of inclination to activate the ball switch inside.
