# Fritzing sketch KY-021 (saved by Fritzing 0.9.3b)

parts:
  Componente1 = Arduino Uno (Rev3)
  Part1 = KY-021 Mini Magnetic Reed Switch Module [package="Breakout board"]

nets:
  N1: Componente1.GND, Part1.-
  N2: Componente1.D3_PWM, Part1.S
  5V: Componente1.5V, Part1.Vin

notes:
  Pin 3 Arduino
  5V Arduino
  Pin central Sensor
  Pin Signal Sensor
  Pin - Sensor
  GND Arduino
  KY-021: Módulo Mini Interruptor reed

custom parts:
  KY-021 Mini Magnetic Reed Switch Module: KY-021 magnetic reed switch module. A reed switch is a magnetic sensor that is normally open and gets closed when exposed to a magnetic field.
