# Fritzing sketch KY-021pi (saved by Fritzing 0.9.3b)

parts:
  Part1 = KY-021 Mini Magnetic Reed Switch Module [package="Breakout board"]
  Raspberry_Pi_1 = Raspberry Pi 3 [part_number=RPI-3-V1.2]

nets:
  N1: Part1.S, Raspberry_Pi_1.GIPO24
  VIN: Part1.Vin, Raspberry_Pi_1.3v3
  N2: Part1.-, Raspberry_Pi_1.GND

notes:
  Pin 18 GPIO24 Raspberry Pi
  Pin 1 3.3V Raspberry Pi
  Pin central Sensor
  Pin Signal Sensor
  Pin - Sensor
  Pin 6 GND Raspberry Pi
  KY-021: Módulo Mini Interruptor reed

custom parts:
  KY-021 Mini Magnetic Reed Switch Module: KY-021 magnetic reed switch module. A reed switch is a magnetic sensor that is normally open and gets closed when exposed to a magnetic field.
