# Fritzing sketch KY-022 (saved by Fritzing 0.9.3b)

parts:
  Componente1 = Arduino Uno (Rev3)
  Part1 = KY-022 Infrared Receiver Module [package="Breakout board"]

nets:
  N1: Componente1.D11_PWM/MOSI, Part1.S
  N2: Componente1.GND, Part1.-
  5V: Componente1.5V, Part1.Vin

notes:
  Pin 11 Arduino
  5V Arduino
  Pin central Sensor
  Pin Signal Sensor
  Pin - Sensor
  GND Arduino
  KY-022: Módulo receptor de infrarrojos

custom parts:
  KY-022 Infrared Receiver Module: Arduino IR receiver module KY-022, reacts to 38kHz infrared light.
