# Fritzing sketch KY-022pi (saved by Fritzing 0.9.3b)

parts:
  Part1 = KY-022 Infrared Receiver Module [package="Breakout board"]
  Raspberry_Pi_1 = Raspberry Pi 3 [part_number=RPI-3-V1.2]

nets:
  N1: Part1.S, Raspberry_Pi_1.GIPO18
  VIN: Part1.Vin, Raspberry_Pi_1.3v3
  N2: Part1.-, Raspberry_Pi_1.GND

notes:
  Pin 12 GPIO18 Raspberry Pi
  Pin 1 3.3V Raspberry Pi
  Pin central Sensor
  Pin Signal Sensor
  Pin - Sensor
  Pin 6 GND Raspberry Pi
  KY-022: Módulo receptor de infrarrojos

custom parts:
  KY-022 Infrared Receiver Module: Arduino IR receiver module KY-022, reacts to 38kHz infrared light.
