# Fritzing sketch KY-023 (saved by Fritzing 0.9.3b)

parts:
  Componente1 = Arduino Uno (Rev3)
  Part1 = KY-023 Dual Axis Joystick Module [package="Breakout board"]

nets:
  N1: Componente1.A0, Part1.VRx
  N2: Componente1.A1, Part1.VRy
  GND: Componente1.GND, Part1.GND
  N3: Componente1.D7, Part1.SW
  5V: Componente1.5V, Part1.+5V

notes:
  Pin A0 Arduino
  5V Arduino
  Pin 5V Sensor
  Pin VRx Sensor
  Pin GND Sensor
  GND Arduino
  KY-023: Módulo Joystick dual axis
  Pin VRy Sensor
  Pin SW Sensor
  Pin A1 Arduino
  Pin 7 Arduino
