# Fritzing sketch KY-023pi (saved by Fritzing 0.9.3b)

parts:
  Part1 = KY-023 Dual Axis Joystick Module [package="Breakout board"]
  Raspberry_Pi_1 = Raspberry Pi 3 [part_number=RPI-3-V1.2]
  Componente1 = Adafruit ADS1115 16Bit I2C ADC [part_number="Adafruit #1085"]

nets:
  GND: Part1.GND, Raspberry_Pi_1.GND, Componente1.GND
  3V3: Part1.+5V, Raspberry_Pi_1.3v3, Raspberry_Pi_1.3V3, Componente1.VDD
  N1: Part1.VRx, Componente1.AIN0
  N2: Part1.VRy, Componente1.AIN1
  N3: Part1.SW, Raspberry_Pi_1.GIPO24
  N4: Raspberry_Pi_1.GPIO2, Componente1.SDA
  N5: Raspberry_Pi_1.GPIO3, Componente1.SCL

notes:
  Pin A0 ADS1115
  Pin 17 3.3V Raspberry Pi
  Pin 5V Sensor
  Pin VRx Sensor
  Pin GND Sensor
  Pin 6 GND Raspberry Pi
  KY-023: Módulo Joystick dual axis
  Pin VRy Sensor
  Pin SW Sensor
  Pin A1 ADS1115
  Pin 18 GPIO24 Raspberry Pi
  Pin 1 3.3V Raspberry Pi
  Pin 9 GND Raspberry Pi
  Pin VDD ADS1115
  Pin GND ADS1115
  Pin SCL ADS1115
  Pin SDA ADS1115
  Pin 3 GPIO2 Raspberry Pi
  Pin 5 GPIO3 Raspberry Pi

custom parts:
  Adafruit ADS1115 16Bit I2C ADC: For microcontrollers without an analog-to-digital converter or when you want a higher-precision ADC, the ADS1115 provides 16-bit precision at 860 samples/second over I2C. The chip can be configured as 4 single-ended input channels, or two differential channels. As a nice bonus, it even includes a programmable gain amplifier, up to x16, to help boost up smaller single/differential signals to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
