# Fritzing sketch KY-024 (saved by Fritzing 0.9.3b)

parts:
  Componente1 = Arduino Uno (Rev3)
  Part1 = KY-024 Linear Hall Magnetic Sensor Module [package="Breakout board"]

nets:
  N1: Componente1.A0, Part1.A0
  N2: Componente1.GND, Part1.G
  N3: Componente1.D3_PWM, Part1.D0
  N4: Componente1.5V, Part1.+

notes:
  Pin 3 Arduino
  5V Arduino
  Pin + Sensor
  Pin D0 Sensor
  Pin G Sensor
  GND Arduino
  KY-024: Módulo Sensor linear efecto Hall
  Pin A0 Sensor
  Pin A0 Arduino

custom parts:
  KY-024 Linear Hall Magnetic Sensor Module: KEYES KY-024 Arduino Linear Hall Magnetic Sensor Module reacts iin the presence of a magnetic field.
