# Fritzing sketch KY-024pi (saved by Fritzing 0.9.3b)

parts:
  Raspberry_Pi_1 = Raspberry Pi 3 [part_number=RPI-3-V1.2]
  Componente1 = Adafruit ADS1115 16Bit I2C ADC [part_number="Adafruit #1085"]
  Part1 = KY-024 Linear Hall Magnetic Sensor Module [package="Breakout board"]

nets:
  3V3: Raspberry_Pi_1.3v3, Raspberry_Pi_1.3V3, Componente1.VDD, Part1.+
  N1: Raspberry_Pi_1.GPIO2, Componente1.SDA
  N2: Raspberry_Pi_1.GPIO3, Componente1.SCL
  GND: Raspberry_Pi_1.GND, Componente1.GND, Part1.G
  N3: Raspberry_Pi_1.GIPO24, Part1.D0
  N4: Componente1.AIN0, Part1.A0

notes:
  Pin 17 3.3V Raspberry Pi
  Pin + Sensor
  Pin GND Sensor
  Pin 6 GND Raspberry Pi
  KY-024: Módulo Sensor linear efecto Hall
  Pin A0 Sensor
  Pin D0 Sensor
  Pin A0 ADS1115
  Pin 18 GPIO24 Raspberry Pi
  Pin 1 3.3V Raspberry Pi
  Pin 9 GND Raspberry Pi
  Pin VDD ADS1115
  Pin GND ADS1115
  Pin SCL ADS1115
  Pin SDA ADS1115
  Pin 3 GPIO2 Raspberry Pi
  Pin 5 GPIO3 Raspberry Pi

custom parts:
  Adafruit ADS1115 16Bit I2C ADC: For microcontrollers without an analog-to-digital converter or when you want a higher-precision ADC, the ADS1115 provides 16-bit precision at 860 samples/second over I2C. The chip can be configured as 4 single-ended input channels, or two differential channels. As a nice bonus, it even includes a programmable gain amplifier, up to x16, to help boost up smaller single/differential signals to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
  KY-024 Linear Hall Magnetic Sensor Module: KEYES KY-024 Arduino Linear Hall Magnetic Sensor Module reacts iin the presence of a magnetic field.
