# Fritzing sketch KY-025 (saved by Fritzing 0.9.3b)

parts:
  Componente1 = Arduino Uno (Rev3)
  Part1 = KY-025 Reed Switch Module [package="Breakout board"]

nets:
  N1: Componente1.A0, Part1.A0
  N2: Componente1.GND, Part1.G
  N3: Componente1.D3_PWM, Part1.D0
  N4: Componente1.5V, Part1.+

notes:
  Pin 3 Arduino
  5V Arduino
  Pin + Sensor
  Pin D0 Sensor
  Pin G Sensor
  GND Arduino
  KY-025: Módulo Interruptor reed
  Pin A0 Sensor
  Pin A0 Arduino

custom parts:
  KY-025 Reed Switch Module: KEYES KY-025 Arduino Reed Switch Module reacts iin the presence of a magnetic field.
