# Fritzing sketch KY-027 (saved by Fritzing 0.9.3b)

parts:
  Componente1 = Arduino Uno (Rev3)
  Part1 = KY-027 Magic Light Cup Module [package="Breakout board"]

nets:
  N1: Componente1.D8, Part1.S
  N2: Componente1.D9_PWM, Part1.L
  N3: Componente1.GND, Part1.G
  N4: Componente1.5V, Part1.+

notes:
  Pin 9 Arduino
  5V Arduino
  Pin + Sensor
  Pin L Sensor
  Pin G Sensor
  GND Arduino
  KY-027: Módulo Taza mágica de luz o Interruptor de mercurio con Led
  Pin S Sensor
  Pin 8 Arduino

custom parts:
  KY-027 Magic Light Cup Module: Arduino KY-0127 magic light cup module is a set of two boards, each one has a led and a mercury tilt switch. Using PWM to drive the LEDs on each module you can achieve the effect of light being "magically" transferred from one module to the other when tilting them.
