# Fritzing sketch KY-027pi (saved by Fritzing 0.9.3b)

parts:
  Part1 = KY-027 Magic Light Cup Module [package="Breakout board"]
  Raspberry_Pi_1 = Raspberry Pi 3 [part_number=RPI-3-V1.2]

nets:
  N1: Part1.G, Raspberry_Pi_1.GND
  N2: Part1.+, Raspberry_Pi_1.3v3
  N3: Part1.S, Raspberry_Pi_1.GIPO24
  N4: Part1.L, Raspberry_Pi_1.GIPO23

notes:
  Pin 16 GPIO23 Raspberry Pi
  Pin 1 3.3V Raspberry Pi
  Pin + Sensor
  Pin L Sensor
  Pin G Sensor
  Pin 6 GND Raspberry Pi
  KY-027: Módulo Taza mágica de luz o Interruptor de mercurio con Led
  Pin S Sensor
  Pin 18 GPIO24 Raspberry Pi

custom parts:
  KY-027 Magic Light Cup Module: Arduino KY-0127 magic light cup module is a set of two boards, each one has a led and a mercury tilt switch. Using PWM to drive the LEDs on each module you can achieve the effect of light being "magically" transferred from one module to the other when tilting them.
