# Fritzing sketch KY-028 (saved by Fritzing 0.9.3b)

parts:
  Componente1 = Arduino Uno (Rev3)
  Part2 = KY-028 Digital Sensor Temperature Module [package="Breakout board"]

nets:
  N1: Componente1.A0, Part2.A0
  N2: Componente1.GND, Part2.G
  N3: Componente1.D3_PWM, Part2.D0
  N4: Componente1.5V, Part2.+

notes:
  Pin 3 Arduino
  5V Arduino
  Pin + Sensor
  Pin D0 Sensor
  Pin G Sensor
  GND Arduino
  KY-028: Módulo Sensor digital de temperatura termistor
  Pin A0 Sensor
  Pin A0 Arduino

custom parts:
  KY-028 Digital Sensor Temperature Module: KEYES KY-026 Arduino Flame Sensor Module reacts iin the presence of fire.
