# Fritzing sketch KY-029 (saved by Fritzing 0.9.3b)

parts:
  Componente1 = Arduino Uno (Rev3)
  Part1 = KY-011 Two Color LED Module [package="Breakout board"]

nets:
  N1: Componente1.D10_PWM/SS, Part1.S
  N2: Componente1.D11_PWM/MOSI, Part1.Vin
  N3: Componente1.GND, Part1.-

notes:
  Pin 10 Arduino
  Pin 11 Arduino
  Pin central Sensor
  Pin Signal Sensor
  Pin - Sensor
  GND Arduino
  KY-029: Módulo Led Bicolor 3mm

custom parts:
  KY-011 Two Color LED Module: KEYES KY-011 Two Color LED Module consist of a common cathode 3mm red/green LED.
