# Fritzing sketch KY-029pi (saved by Fritzing 0.9.3b)

parts:
  Part1 = KY-011 Two Color LED Module [package="Breakout board"]
  Raspberry_Pi_1 = Raspberry Pi 3 [part_number=RPI-3-V1.2]

nets:
  N1: Part1.S, Raspberry_Pi_1.GIPO23
  N2: Part1.Vin, Raspberry_Pi_1.GIPO18
  N3: Part1.-, Raspberry_Pi_1.GND

notes:
  Pin 16 GPIO23 Raspberry Pi
  Pin 12 GPIO18 Raspberry Pi
  Pin central Sensor
  Pin Signal Sensor
  Pin - Sensor
  Pin 6 GND Raspberry Pi
  KY-029: Módulo Led Bicolor 3mm

custom parts:
  KY-011 Two Color LED Module: KEYES KY-011 Two Color LED Module consist of a common cathode 3mm red/green LED.
