# Fritzing sketch KY-032 (saved by Fritzing 0.9.3b)

parts:
  M1 = fc-51 [package=THT]
  Part1 = Arduino Uno (Rev3)

nets:
  N1: M1.pin1, Part1.D10_PWM/SS
  N2: M1.pin2, Part1.GND
  N3: M1.pin3, Part1.5V

notes:
  VCC
  5V
  OUT
  Pin 10
  GND
  KY-032: Módulo Sensor de obstáculos
