# Fritzing sketch KY-032pi (saved by Fritzing 0.9.3b)

parts:
  M1 = fc-51 [package=THT]
  Raspberry_Pi_1 = Raspberry Pi 3 [part_number=RPI-3-V1.2]

nets:
  N1: M1.pin1, Raspberry_Pi_1.GIPO24
  N2: M1.pin2, Raspberry_Pi_1.GND
  N3: M1.pin3, Raspberry_Pi_1.3v3

notes:
  VCC
  Pin 1 3.3V
  OUT
  GPIO 24 Pin fisico 18
  GND Pin 6
  GND
  KY-032: Módulo Sensor de obstáculos
