# Fritzing sketch KY-033 (saved by Fritzing 0.9.3b)

parts:
  Componente1 = Arduino Uno (Rev3)
  Componente2 = KY-033 Tracing Black White Line Hunting Sensor Module For Arduino

nets:
  GND: Componente1.GND, Componente2.GND
  N1: Componente1.D3_PWM, Componente2.S
  N2: Componente1.5V, Componente2.V+

notes:
  Pin 3 Arduino
  5V Arduino
  Pin V+ Sensor
  Pin S Sensor
  Pin G Sensor
  GND Arduino
  KY-033: Módulo Seguidor de línea

custom parts:
  KY-033 Tracing Black White Line Hunting Sensor Module For Arduino: Tracing Black White Line Hunting Sensor Module For Arduino Description: This is KY-033 tracking sensor. The KY-033 measures the intensity of infrared radiation and delivers it as an analog output voltage. Features: Operating voltage: 2.5 - 12V(cannot over12V) working current: 18mA-20mA at 5V Enhanced accuracy Documents: http://www.vishay.com/docs/83760/tcrt5000.pdf
