# Fritzing sketch KY-033pi (saved by Fritzing 0.9.3b)
circuit board: 8.46667cm x 5.64444cm

parts:
  Componente2 = KY-033 Tracing Black White Line Hunting Sensor Module For Arduino
  Raspberry_Pi_1 = Raspberry Pi 3 [part_number=RPI-3-V1.2]

nets:
  GND: Componente2.GND, Raspberry_Pi_1.GND
  N1: Componente2.V+, Raspberry_Pi_1.3v3
  N2: Componente2.S, Raspberry_Pi_1.GIPO24

notes:
  Pin 18 GPIO24 Raspberry Pi
  Pin 1 3.3V Raspberry Pi
  Pin V+ Sensor
  Pin S Sensor
  Pin G Sensor
  Pin 6 GND Raspberry Pi
  KY-033: Módulo Seguidor de línea

custom parts:
  KY-033 Tracing Black White Line Hunting Sensor Module For Arduino: Tracing Black White Line Hunting Sensor Module For Arduino Description: This is KY-033 tracking sensor. The KY-033 measures the intensity of infrared radiation and delivers it as an analog output voltage. Features: Operating voltage: 2.5 - 12V(cannot over12V) working current: 18mA-20mA at 5V Enhanced accuracy Documents: http://www.vishay.com/docs/83760/tcrt5000.pdf
