# Fritzing sketch KY-034 (saved by Fritzing 0.9.3b)

parts:
  Componente1 = Arduino Uno (Rev3)
  Part1 = KY-005 Infrared Transmitter Module [package="Breakout board"]

nets:
  N1: Componente1.D13/SCK, Part1.S
  N2: Componente1.GND, Part1.-

notes:
  Pin 13 Arduino
  Pin Signal Sensor
  Pin - Sensor
  GND Arduino
  KY-034: Módulo Led THT Flash de 7 colores

custom parts:
  KY-005 Infrared Transmitter Module: Arduino IR Transmitter Module Keyes KY-005, emits infrared light at 38KHz.
