# Fritzing sketch KY-034pi (saved by Fritzing 0.9.3b)

parts:
  Raspberry_Pi_1 = Raspberry Pi 3 [part_number=RPI-3-V1.2]
  Part1 = KY-005 Infrared Transmitter Module [package="Breakout board"]

nets:
  N1: Raspberry_Pi_1.GIPO24, Part1.S
  N2: Raspberry_Pi_1.GND, Part1.-

notes:
  Pin 18 GPIO24 Raspberry Pi
  Pin Signal Sensor
  Pin - Sensor
  Pin 6 GND Raspberry Pi
  KY-034: Módulo LED THT Flash de 7 Colores

custom parts:
  KY-005 Infrared Transmitter Module: Arduino IR Transmitter Module Keyes KY-005, emits infrared light at 38KHz.
