# Fritzing sketch KY-035pi (saved by Fritzing 0.9.3b)

parts:
  Raspberry_Pi_1 = Raspberry Pi 3 [part_number=RPI-3-V1.2]
  Componente1 = Adafruit ADS1115 16Bit I2C ADC [part_number="Adafruit #1085"]
  Part1 = KY-003 Hall Magnetic Sensor Module [package="Breakout board"]

nets:
  3V3: Raspberry_Pi_1.3v3, Raspberry_Pi_1.3V3, Componente1.VDD, Part1.Vin
  N1: Raspberry_Pi_1.GPIO2, Componente1.SDA
  N2: Raspberry_Pi_1.GPIO3, Componente1.SCL
  GND: Raspberry_Pi_1.GND, Componente1.GND, Part1.-
  N3: Componente1.AIN0, Part1.S

notes:
  Pin 1 3.3V Raspberry Pi
  Pin + Sensor
  Pin - Sensor
  Pin 6 GND Raspberry Pi
  KY-035: Módulo Sensor magnético Bihor
  Pin S Sensor
  Pin 17 3.3V Raspberry Pi
  Pin A0 ADS1115
  Pin GND ADS1115
  Pin VDD ADS1115
  Pin SCL ADS115
  Pin SDA ADS115
  Pin 3 GPIO2 Raspberry Pi
  Pin 5 GPIO3 Raspberry Pi
  Pin 9 GND Raspberry Pi
  KY-053 ADS1115

custom parts:
  Adafruit ADS1115 16Bit I2C ADC: For microcontrollers without an analog-to-digital converter or when you want a higher-precision ADC, the ADS1115 provides 16-bit precision at 860 samples/second over I2C. The chip can be configured as 4 single-ended input channels, or two differential channels. As a nice bonus, it even includes a programmable gain amplifier, up to x16, to help boost up smaller single/differential signals to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
  KY-003 Hall Magnetic Sensor Module: KEYES KY-003 Arduino Hall Magnetic Sensor Module is a switch that will turn on/off in the presence of a magnetic field.
