# Fritzing sketch KY-036 (saved by Fritzing 0.9.3b)

parts:
  Componente1 = Arduino Uno (Rev3)
  Part1 = KY-028 Digital Sensor Temperature Module [package="Breakout board"]
  U1 = TL431 [package="TO92 (THT)"]  # not connected

nets:
  N1: Componente1.GND, Part1.G
  N2: Componente1.D0/RX, Part1.A0
  N3: Componente1.D3_PWM, Part1.D0
  N4: Componente1.5V, Part1.+

notes:
  Pin 3 Arduino
  5V Arduino
  Pin + Sensor
  Pin D0 Sensor
  Pin G Sensor
  GND Arduino
  KY-036: Módulo Táctil metálico
  Pin A0 Sensor
  Pin 0 Arduino

custom parts:
  KY-028 Digital Sensor Temperature Module: KEYES KY-026 Arduino Flame Sensor Module reacts iin the presence of fire.
  TL431: 2% accuracy adjustable precision shunt regulator
