# Fritzing sketch KY-036pi (saved by Fritzing 0.9.3b)

parts:
  Part1 = KY-028 Digital Sensor Temperature Module [package="Breakout board"]
  U1 = TL431 [package="TO92 (THT)"]  # not connected
  Componente1 = Adafruit ADS1115 16Bit I2C ADC [part_number="Adafruit #1085"]
  Raspberry_Pi_1 = Raspberry Pi 3 [part_number=RPI-3-V1.2]

nets:
  N1: Part1.A0, Componente1.AIN0
  GND: Part1.G, Componente1.GND, Raspberry_Pi_1.GND
  3V3: Part1.+, Componente1.VDD, Raspberry_Pi_1.3v3, Raspberry_Pi_1.3V3
  N2: Part1.D0, Raspberry_Pi_1.GIPO24
  N3: Componente1.SDA, Raspberry_Pi_1.GPIO2
  N4: Componente1.SCL, Raspberry_Pi_1.GPIO3

notes:
  Pin 18 GPIO24 Raspberry Pi
  Pin 1 3.3V Raspberry Pi
  Pin + Sensor
  Pin D0 Sensor
  Pin G Sensor
  Pin 6 GND Raspberry Pi
  KY-036: Módulo Táctil metálico
  Pin A0 Sensor
  Pin A0 ADS1115
  Pin 17 3.3V Raspberry Pi
  Pin 9 GND Raspberry Pi
  Pin 5 GPIO3 Raspberry Pi
  Pin 3 GPIO2 Raspberry Pi
  SDA ADS1115
  SCL ADS1115
  GND ADS1115
  VDD ADS1115
  KY-053 ADS1115

custom parts:
  KY-028 Digital Sensor Temperature Module: KEYES KY-026 Arduino Flame Sensor Module reacts iin the presence of fire.
  TL431: 2% accuracy adjustable precision shunt regulator
  Adafruit ADS1115 16Bit I2C ADC: For microcontrollers without an analog-to-digital converter or when you want a higher-precision ADC, the ADS1115 provides 16-bit precision at 860 samples/second over I2C. The chip can be configured as 4 single-ended input channels, or two differential channels. As a nice bonus, it even includes a programmable gain amplifier, up to x16, to help boost up smaller single/differential signals to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
