# Fritzing sketch KY-038 (saved by Fritzing 0.9.3b)

parts:
  Componente1 = Arduino Uno (Rev3)
  Mic1 = KY-038

nets:
  N1: Componente1.GND, Mic1.pin2
  N2: Componente1.D0/RX, Mic1.pin1
  N3: Componente1.D3_PWM, Mic1.pin4
  N4: Componente1.5V, Mic1.pin3

notes:
  Pin 3 Arduino
  5V Arduino
  Pin + Sensor
  Pin D0 Sensor
  Pin G Sensor
  GND Arduino
  KY-038: Módulo Small Sound
  Pin A0 Sensor
  Pin 0 Arduino

custom parts:
  KY-038: ky-038 Microphone sound sensor module
