# Fritzing sketch KY-039 (saved by Fritzing 0.9.3b)

parts:
  Componente1 = Arduino Uno (Rev3)
  Part1 = KY-018 Photoresistor Module [package="Breakout board"]

nets:
  N1: Componente1.GND, Part1.-
  N2: Componente1.D0/RX, Part1.S
  5V: Componente1.5V, Part1.Vin

notes:
  Pin 0 Arduino
  5V Arduino
  Pin central Sensor
  Pin Signal Sensor
  Pin - Sensor
  GND Arduino
  KY-039: Módulo Sensor de latidos bpm

custom parts:
  KY-018 Photoresistor Module: KY-018 Photoresistor module, used to measure light intensity. It can determine the presence or absence of light.
