# Fritzing sketch KY-050 (saved by Fritzing 0.9.3b)

parts:
  Part1 = Arduino Uno (Rev3)
  Part2 = SRF05 Ultrasonic Rangefinder

nets:
  N1: Part1.D8, Part2.Trig
  GND: Part1.GND, Part2.GND
  N2: Part1.D7, Part2.Echo
  5V: Part1.5V, Part2.VCC

notes:
  KY-050: Módulo HC-SR04 Sensor de distancia
  GND
  ECHO
  Pin 7
  VCC
  5V
  TRIGGER
  Pin 8
