# Fritzing sketch KY-050pi (saved by Fritzing 0.9.3b)

parts:
  Part2 = SRF05 Ultrasonic Rangefinder
  Raspberry_Pi_1 = Raspberry Pi 3 [part_number=RPI-3-V1.2]
  R2 = Resistor [tolerance=±5% resistance=1k part_number=1K package=THT]
  R1 = Resistor [tolerance=±5% resistance=2.2k package=THT]

nets:
  VCC: Part2.VCC, Raspberry_Pi_1.5V
  N1: Part2.Trig, Raspberry_Pi_1.GIPO17
  N2: Part2.Echo, R2.Pin_0
  GND: Part2.GND, Raspberry_Pi_1.GND, R1.Pin_1
  N3: Raspberry_Pi_1.GIPO27, R2.Pin_1

notes:
  KY-050: Módulo HC-SR04 Sensor de distancia
  GND
  GND Pin 6
  ECHO
  GPIO 27 Pin fisico 13
  VCC
  5V Pin 2
  TRIGGER
  GPIO 17Pin fisico 11
  GND Pin 20
  2.2kΩ
  1kΩ
