# Fritzing sketch KY-051 (saved by Fritzing 0.9.3b)

parts:
  Raspberry_Pi_1 = Raspberry Pi 3 [part_number=RPI-3-V1.2]
  LLC2 = Logic Level Converter [package="Breakout board"]
  Componente2 = Arduino Uno (Rev3)

nets:
  N1: Raspberry_Pi_1.3v3, LLC2.LV
  N2: Raspberry_Pi_1.GND, LLC2.LV2, LLC2.L-GND
  N3: Raspberry_Pi_1.GIPO14, LLC2.LV1
  N4: LLC2.H-GND, Componente2.GND
  N5: LLC2.HV, Componente2.5V
  N6: LLC2.HV2, Componente2.D1/TX
  N7: LLC2.HV1, Componente2.D0/RX

notes:
  GND
  5V
  3.3V
  HV1 5V
  PIN 8 GPIO14 TX 3.3V
  HV2 5V
  PIN 10 GPIO15 RX 3.3V
  MÓDULO KY-051 voltage translator/Level shifter
  LV2 3.3V
  TX0 5V
  LV1 3.3V
  RX0 5V

custom parts:
  Logic Level Converter: 5V to/from 3.3V logic level converter
