# Fritzing sketch KY-051_PI (saved by Fritzing 0.9.3b)

parts:
  Componente1 = SRF05 Ultrasonic Rangefinder
  Raspberry_Pi_1 = Raspberry Pi 3 [part_number=RPI-3-V1.2]
  LLC2 = Logic Level Converter [package="Breakout board"]

nets:
  VCC: Componente1.VCC, Raspberry_Pi_1.5V, LLC2.HV
  N1: Componente1.Trig, LLC2.HV1
  N2: Componente1.Echo, LLC2.HV2
  N3: Componente1.GND, LLC2.H-GND
  N4: Raspberry_Pi_1.3v3, LLC2.LV
  N5: Raspberry_Pi_1.GPIO3, LLC2.LV2
  N6: Raspberry_Pi_1.GIPO18, LLC2.LV1
  N7: Raspberry_Pi_1.GND, LLC2.L-GND

notes:
  GND
  5V
  3.3V
  VCC
  TRIG 5V
  TRIG 3.3V
  PIN 12 GPIO18
  ECHO 5V
  ECHO 3.3V
  PIN 5 GPIO3
  MÓDULO KY-051 voltage translator/Level shifter

custom parts:
  Logic Level Converter: 5V to/from 3.3V logic level converter
