# Fritzing sketch KY-052 (saved by Fritzing 0.9.3b)

parts:
  Part1 = Adafruit_BMP280
  Part2 = Arduino Uno (Rev3)

nets:
  VIN: Part1.VIN, Part2.5V
  GND: Part1.GND, Part2.GND
  N1: Part1.SCK/SCL, Part2.D13/SCK
  N2: Part1.SDO/ADR, Part2.D12/MISO
  N3: Part1.SDI/SDA, Part2.D11_PWM/MOSI
  N4: Part1.CS, Part2.D10_PWM/SS

notes:
  KY-052: Módulo BMP280
  Pin Vin BMP280
  Pin GND BMP280
  Pin 5V Arduino
  Pin GND Arduino
  Pin SCL/SCK BMP280
  Pin 13 Arduino
  Pin SD0/ADR BMP280
  Pin 12 Arduino
  Pin CS/CSB BMP280
  Pin 10 Arduino
  Pin SDA/SDI BMP280
  Pin 11 Arduino

custom parts:
  Adafruit_BMP280: Bosch has stepped up their game with their new BMP280 sensor, an environmental sensor with temperature, barometric pressure that is the next generation upgrade to the BMP085/BMP180/BMP183. This sensor is great for all sorts of weather sensing and can even be used in both I2C and SPI! This precision sensor from Bosch is the best low-cost, precision sensing solution for measuring barometric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
