# Fritzing sketch KY-052pi (saved by Fritzing 0.9.3b)

parts:
  Part1 = Adafruit_BMP280
  Raspberry_Pi_1 = Raspberry Pi 3 [part_number=RPI-3-V1.2]

nets:
  GND: Part1.GND, Raspberry_Pi_1.GND
  N1: Part1.SCK/SCL, Raspberry_Pi_1.GPIO3
  N2: Part1.SDO/ADR, Raspberry_Pi_1.GIPO23
  N3: Part1.SDI/SDA, Raspberry_Pi_1.GPIO2
  N4: Part1.CS, Raspberry_Pi_1.3v3

notes:
  KY-052: Módulo BMP280
  Pin GND BMP280
  Pin 6 GND
  Pin SCL/SCK BMP280
  Pin 5 GPIO 3 SCL
  Pin SD0/ADR BMP280
  Pin 16 GPIO 23
  Pin CS/CSB BMP280
  Pin 1 3.3V
  Pin SDA/SDI BMP280
  Pin 3 GPIO 2 SDA

custom parts:
  Adafruit_BMP280: Bosch has stepped up their game with their new BMP280 sensor, an environmental sensor with temperature, barometric pressure that is the next generation upgrade to the BMP085/BMP180/BMP183. This sensor is great for all sorts of weather sensing and can even be used in both I2C and SPI! This precision sensor from Bosch is the best low-cost, precision sensing solution for measuring barometric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
