# Fritzing sketch KY-053 (saved by Fritzing 0.9.3b)

parts:
  Componente1 = Adafruit ADS1115 16Bit I2C ADC [part_number="Adafruit #1085"]
  Componente2 = Arduino Uno (Rev3)

nets:
  N1: Componente1.SDA, Componente2.A4/SDA
  N2: Componente1.SCL, Componente2.A5/SCL
  GND: Componente1.GND, Componente2.GND
  VDD: Componente1.VDD, Componente2.5V

notes:
  Pin GND Arduino
  KY-053: Módulo ADS1115 Convertidor Analógico-Digital
  Pines A0,1,2,3,4 ADS1115
  Pin 5V Arduino
  Pin 19/A5 SCL Arduino
  Pin 18/A4 SDA Arduino
  SDA ADS1115
  SCL ADS1115
  GND ADS1115
  VDD ADS1115
  KY-053 ADS1115
  Pin de Señal de Dispositivo analógico

custom parts:
  Adafruit ADS1115 16Bit I2C ADC: For microcontrollers without an analog-to-digital converter or when you want a higher-precision ADC, the ADS1115 provides 16-bit precision at 860 samples/second over I2C. The chip can be configured as 4 single-ended input channels, or two differential channels. As a nice bonus, it even includes a programmable gain amplifier, up to x16, to help boost up smaller single/differential signals to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
