# Fritzing sketch KY-053pi (saved by Fritzing 0.9.3b)

parts:
  Componente1 = Adafruit ADS1115 16Bit I2C ADC [part_number="Adafruit #1085"]
  Raspberry_Pi_1 = Raspberry Pi 3 [part_number=RPI-3-V1.2]

nets:
  N1: Componente1.SDA, Raspberry_Pi_1.GPIO2
  N2: Componente1.SCL, Raspberry_Pi_1.GPIO3
  GND: Componente1.GND, Raspberry_Pi_1.GND
  VDD: Componente1.VDD, Raspberry_Pi_1.3V3

notes:
  Pin 6 GND Raspberry Pi
  KY-053: Módulo ADS1115 Convertidor Analógico-Digital
  Pines A0,1,2,3,4 ADS1115
  Pin 17 3.3V Raspberry Pi
  Pin 5 GPIO3 Raspberry Pi
  Pin 3 GPIO2 Raspberry Pi
  SDA ADS1115
  SCL ADS1115
  GND ADS1115
  VDD ADS1115
  KY-053 ADS1115
  Pin de Señal de Dispositivo analógico

custom parts:
  Adafruit ADS1115 16Bit I2C ADC: For microcontrollers without an analog-to-digital converter or when you want a higher-precision ADC, the ADS1115 provides 16-bit precision at 860 samples/second over I2C. The chip can be configured as 4 single-ended input channels, or two differential channels. As a nice bonus, it even includes a programmable gain amplifier, up to x16, to help boost up smaller single/differential signals to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
