# Fritzing sketch KY_039_Arduino (saved by Fritzing 0.9.10b)

parts:
  Componente1 = Arduino Uno (Rev3)
  A1 = KY-039 [package=THT]

nets:
  N1: Componente1.A0, A1.pin1
  N2: Componente1.5V, A1.pin2
  N3: Componente1.GND, A1.pin3

notes:
  KY-039: Sensor de latidos BPM
  Raspberry Pi Buenos Aires
  Pin(-)GND
  Pin(S)Signal
  Pin(Central)VCC
  Pin A0
  Pin GND
  Pin 5V

custom parts:
  KY-039: KY-039 heart beat sensor.
