# Fritzing sketch KY_039_RaspberryPi (saved by Fritzing 0.9.10b)

parts:
  A1 = KY-039 [package=THT]
  Mod1 = Raspberry Pi 4B
  Componente1 = Adafruit ADS1115 16Bit I2C ADC [part_number="Adafruit #1085"]

nets:
  N1: A1.pin1, Componente1.AIN0, Componente1.ALERT
  3V3: A1.pin2, Mod1.3V3, Componente1.VDD
  GND: A1.pin3, Mod1.GND, Componente1.GND
  N2: Mod1.GPIO2, Componente1.SDA
  N3: Mod1.GPIO3, Componente1.SCL

notes:
  KY-039: Sensor de latidos BPM
  Raspberry Pi Buenos Aires
  Pin(-)GND
  Pin(S)Signal
  Pin(Central)VCC
  Pin A0
  Pin GND
  Pin 17 3V3
  Pin(VDD)
  Pin 6 GND
  Pin 1 3V3
  Pin 9 GND
  Pin 3 GPIO2
  Pin 5 GPIO3
  Pin SDA
  Pin SCL

custom parts:
  KY-039: KY-039 heart beat sensor.
  Adafruit ADS1115 16Bit I2C ADC: For microcontrollers without an analog-to-digital converter or when you want a higher-precision ADC, the ADS1115 provides 16-bit precision at 860 samples/second over I2C. The chip can be configured as 4 single-ended input channels, or two differential channels. As a nice bonus, it even includes a programmable gain amplifier, up to x16, to help boost up smaller single/differential signals to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
