# Fritzing sketch KY_039_RP2040W (saved by Fritzing 0.9.10b)

parts:
  A1 = KY-039 [package=THT]
  Mod1 = Raspberry Pi Pico W

nets:
  N1: A1.pin1, Mod1.pin_31
  N2: A1.pin2, Mod1.pin_36
  N3: A1.pin3, Mod1.pin_28, Mod1.pin_33

notes:
  KY-039: Sensor de latidos BPM
  Raspberry Pi Buenos Aires
  Pin(-)GND
  Pin(S)Signal
  Pin(Central)VCC
  Pin 31 GP26 ADC0
  Pin 28 GND
  Pin 36 3V3 OUT

custom parts:
  KY-039: KY-039 heart beat sensor.
  Raspberry Pi Pico W: Raspberry Pi Pico W. Based around the RP2040 microcontroller the Pico W is a low cost microcontroller device bringing Raspberry Pi quality, cost, and easy of use to the microcontroller space. The areas marked KEEPOUT in pcb silkscreen should not have traces running through them to avoid shorts on a soldered in module!
