# Fritzing sketch KY_039_RP2040 (saved by Fritzing 0.9.10b)

parts:
  A1 = KY-039 [package=THT]
  Mod3 = Raspberry Pi Pico

nets:
  N1: A1.pin1, Mod3.pin_31
  N2: A1.pin2, Mod3.pin_36
  N3: A1.pin3, Mod3.pin_23, Mod3.pin_28, Mod3.pin_33

notes:
  KY-039: Sensor de latidos BPM
  Raspberry Pi Buenos Aires
  Pin(-)GND
  Pin(S)Signal
  Pin(Central)VCC
  Pin 31 GP26 ADC0
  Pin 28 GND
  Pin 36 3V3 OUT

custom parts:
  KY-039: KY-039 heart beat sensor.
  Raspberry Pi Pico: Raspberry Pi Pico. Based around the RP2040 microcontroller the Pico is a low cost microcontroller device bringing Raspberry Pi quality, cost, and easy of use to the microcontroller space. Jan 2021, Split part in to two versions: SMD (this one) and tht. This one is single sided and uses the castellation pads to solder the module to the board (no holes, other than for the USB connector!). The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
